# Fritzing sketch Serra (saved by Fritzing 0.9.10b)
circuit board: 8.46667cm x 5.64444cm
breadboards: 1

parts:
  Display = Grove OLED 128x96
  Soil = Soil Moisture Sensor
  Part2 = Arduino Uno (Rev3)
  R2 = Resistor [tolerance=±5% resistance=10k package="0603 [SMD]"]
  Photoresistor = PHOTOCELL [package=photocell-kit]
  LED_strip = WS2812 RGB LED matrix 1x8
  S1 = Taiway 100-SP-X-T1 SPDT Miniature Toggle Switch [part_number=100-SP-X-T1-0-0-B1-M1 package=THT]
  Water_Pump = water pump/motor  # not connected
  Temperature = Humidity and Temperature Sensor RHT03
  RelayFan1 = KY-019 5V Relay Module [package="Breakout board"]
  RelayFan2 = KY-019 5V Relay Module [package="Breakout board"]
  Fan1 = DC Motor [voltage_(max)=6V voltage_(min)=3V]
  Fan2 = DC Motor [voltage_(max)=6V voltage_(min)=3V]
  RelayPump = KY-019 5V Relay Module [package="Breakout board"]
  R3 = Resistor [tolerance=±5% power=0.25 resistance=220 package=THT]

nets:
  GND: Display.GND, Soil.GND, Part2.GND, R2.Pin_0, LED_strip.GND, S1.COM, Temperature.GND_1, RelayFan1.-, RelayFan2.-, RelayPump.-
  VCC: Display.VCC, Soil.VCC, Part2.5V, Photoresistor.P$1, S1.L2, Temperature.Vcc, RelayFan1.+, RelayFan2.+, RelayPump.+
  N1: Display.SDA, Part2.A4/SDA
  N2: Display.SCL, Part2.A5/SCL
  N3: Soil.SIG, Part2.A1
  N4: Part2.A0, R2.Pin_1, Photoresistor.P$2
  N5: Part2.D12/MISO, Temperature.Data-signal
  N6: Part2.D13/SCK, RelayFan1.S, RelayFan2.S
  N7: Part2.D2, R3.Pin_1
  N8: Part2.D3_PWM, RelayPump.S
  N9: LED_strip.VCC, S1.L1
  N10: LED_strip.DIN, R3.Pin_0
  N11: RelayFan1.Common, Fan1.pin_1
  N12: RelayFan1.NO, Fan1.pin_2
  N13: RelayFan2.Common, Fan2.pin_1
  N14: RelayFan2.NO, Fan2.pin_2

notes:
  switch
  vento
  Sensori
  Attuatori

custom parts:
  WS2812 RGB LED matrix 1x8: WS2812 matrix 1x8
  water pump/motor: WATER PUMP BY ARDUBLOCKTR
  KY-019 5V Relay Module: KY-019 5V Relay module, used to control AC circuits. (Special thanks to vanepp for fixing the PCB holes and other errors)
